# Fritzing sketch Sketch (saved by Fritzing 0.9.2b)
breadboards: 1

parts:
  ESP8266-1 = ESP8266-12 [part_number=ESP8266-12]
  R1 = Resistor [tolerance=±5% resistance=10k package=THT]
  R2 = Resistor [tolerance=±5% resistance=10k package=THT]
  R4 = Resistor [tolerance=±5% resistance=470 package=THT]
  J1 = male pin header, 3 pins [form="♂ (male)"]
  J2 = male pin header, 3 pins [form="♂ (male)"]
  R5 = Resistor [tolerance=±5% resistance=10k package=THT]

nets:
  N1: ESP8266-1.REST, R1.Pin_1, R4.Pin_0
  N2: ESP8266-1.CH_PD, R2.Pin_1
  N3: ESP8266-1.GPIO16, R4.Pin_1
  N4: ESP8266-1.VCC, R1.Pin_0, R2.Pin_0
  N5: ESP8266-1.TXD, J1.pin1
  N6: ESP8266-1.RXD, J1.pin2
  N7: ESP8266-1.GPIO2, J2.pin2
  N8: ESP8266-1.GPIO15, R5.Pin_1
  N9: ESP8266-1.GND, J1.pin3, J2.pin3
